# Fritzing sketch hatten2-1-2 (saved by Fritzing 0.9.3b)
breadboards: 1

parts:
  パーツ2 = Arduino Uno (Rev3)
  S1 = Pushbutton [package="[THT]"]
  S2 = Pushbutton [package="[THT]"]
  S3 = Pushbutton [package="[THT]"]
  R1 = Resistor [tolerance=±5% resistance=1k package=THT]
  R2 = Resistor [tolerance=±5% resistance=1k package=THT]
  R3 = Resistor [tolerance=±5% resistance=1k package=THT]
  LED1 = RGB LED (com. anode, rbg) [package="5 mm [THT]"]

nets:
  N1: パーツ2.GND, LED1.blue_cathode
  N2: パーツ2.5V, S1.Pin_3, S1.Pin_4, S2.Pin_3, S2.Pin_4, S3.Pin_3, S3.Pin_4
  N3: S1.Pin_1, S1.Pin_2, R2.Pin_1
  N4: S2.Pin_1, S2.Pin_2, R3.Pin_1
  N5: S3.Pin_1, S3.Pin_2, R1.Pin_1
  N6: R1.Pin_0, LED1.red_cathode
  N7: R2.Pin_0, LED1.green_cathode
  N8: R3.Pin_0, LED1.common_anode
