# Fritzing sketch hatten2-3-1 (saved by Fritzing 0.9.3b)
breadboards: 1

parts:
  パーツ1 = Arduino Uno (Rev3)
  J1 = Piezo Speaker
  R1 = Resistor [tolerance=±5% resistance=330 package=THT]

nets:
  N1: パーツ1.D9_PWM, R1.Pin_0
  N2: パーツ1.GND, J1.pin1
  N3: J1.pin2, R1.Pin_1
