# Fritzing sketch kadai2-3-2 (saved by Fritzing 0.9.3b)
breadboards: 1

parts:
  パーツ1 = Arduino Uno (Rev3)
  R2 = PHOTOCELL [package=photocell-kit]
  R3 = Resistor [tolerance=±5% resistance=10k package=THT]
  LED1 = LED - 5mm [color="Red (633nm)" package="5 mm [THT]"]
  R4 = Resistor [tolerance=±5% resistance=330 package=THT]

nets:
  N1: パーツ1.A0, R2.P$2, R3.Pin_0
  N2: パーツ1.D3_PWM, R4.Pin_0
  N3: パーツ1.5V, R2.P$1
  N4: パーツ1.GND, R3.Pin_1, LED1.cathode
  N5: LED1.anode, R4.Pin_1
