# Fritzing sketch kadai7-1-4 (saved by Fritzing 0.9.3b)
breadboards: 1

parts:
  パーツ1 = Arduino Uno (Rev3)
  パーツ2 = SRF05 Ultrasonic Rangefinder
  R1 = Resistor [tolerance=±5% resistance=330 package=THT]
  LED1 = smd LED [color="Red (633nm)" package="0805 [SMD]"]
  J1 = Piezo Speaker
  R2 = Resistor [tolerance=±5% resistance=330 package=THT]

nets:
  N1: パーツ1.D8, パーツ2.Echo
  N2: パーツ1.D9_PWM, R2.Pin_0
  N3: パーツ1.D4, R1.Pin_0
  N4: パーツ1.D7, パーツ2.Trig
  5V: パーツ1.5V, パーツ2.VCC
  GND: パーツ1.GND, パーツ2.GND, LED1.cathode, J1.pin1
  N5: R1.Pin_1, LED1.anode
  N6: J1.pin2, R2.Pin_1
