# Fritzing sketch hatten2-1-1 (saved by Fritzing 0.9.3b)
breadboards: 1

parts:
  パーツ1 = Arduino Uno (Rev3)
  R1 = Resistor [tolerance=±5% resistance=330 package=THT]
  R2 = Resistor [tolerance=±5% resistance=510 package=THT]
  R3 = Resistor [tolerance=±5% resistance=1k package=THT]
  LED1 = LED - 5mm [color="Red (633nm)" package="5 mm [THT]"]

nets:
  N1: パーツ1.GND, LED1.cathode
  N2: パーツ1.5V, R1.Pin_0
  N3: R1.Pin_1, R2.Pin_0, R3.Pin_0
  N4: R2.Pin_1, R3.Pin_1, LED1.anode
