# Fritzing sketch kadai2-2-1 (saved by Fritzing 0.9.3b)
breadboards: 1

parts:
  パーツ1 = Arduino Uno (Rev3)
  S1 = Pushbutton [package="[THT]"]
  R1 = Resistor [tolerance=±5% resistance=220 package=THT]
  LED1 = LED - 5mm [color="Red (633nm)" package="5 mm [THT]"]
  R2 = Resistor [tolerance=±5% resistance=330 package=THT]

nets:
  N1: パーツ1.D13/SCK, R2.Pin_0
  N2: パーツ1.GND, S1.Pin_1, S1.Pin_2, LED1.cathode
  N3: パーツ1.D4, S1.Pin_3, S1.Pin_4, R1.Pin_1
  N4: パーツ1.5V, R1.Pin_0
  N5: LED1.anode, R2.Pin_1
