# Fritzing sketch kadai2-2-4 (saved by Fritzing 0.9.3b)
breadboards: 1

parts:
  パーツ1 = Arduino Uno (Rev3)
  S1 = Pushbutton [package="[THT]"]
  R1 = Resistor [tolerance=±5% resistance=220 package=THT]
  LED1 = LED - 5mm [color="Red (633nm)" package="5 mm [THT]"]
  R2 = Resistor [tolerance=±5% resistance=330 package=THT]
  R3 = Resistor [tolerance=±5% resistance=330 package=THT]
  LED2 = LED - 5mm [color="Yellow (592nm)" package="5 mm [THT]"]

nets:
  N1: パーツ1.D13/SCK, R3.Pin_0
  N2: パーツ1.GND, S1.Pin_1, S1.Pin_2, LED1.cathode, LED2.cathode
  N3: パーツ1.D3_PWM, R2.Pin_0
  N4: パーツ1.D4, S1.Pin_3, S1.Pin_4, R1.Pin_1
  N5: パーツ1.5V, R1.Pin_0
  N6: LED1.anode, R2.Pin_1
  N7: R3.Pin_1, LED2.anode
