# Fritzing sketch enshu2-3-4 (saved by Fritzing 0.9.3b)
breadboards: 1

parts:
  パーツ1 = Arduino Uno (Rev3)
  R1 = Resistor [tolerance=±5% resistance=330 package=THT]
  LED1 = LED - 5mm [color="Red (633nm)" package="5 mm [THT]"]
  R2 = Resistor [tolerance=±5% resistance=330 package=THT]
  LED3 = LED - 5mm [color="Red (633nm)" package="5 mm [THT]"]

nets:
  N1: パーツ1.D9_PWM, R1.Pin_0
  N2: パーツ1.D11_PWM/MOSI, R2.Pin_0
  N3: パーツ1.GND, LED1.cathode, LED3.cathode
  N4: R1.Pin_1, LED1.anode
  N5: R2.Pin_1, LED3.anode
