# Fritzing sketch kadai2-3-1 (saved by Fritzing 0.9.3b)
breadboards: 1

parts:
  パーツ1 = Arduino Uno (Rev3)
  R1 = Trimmer Potentiometer [maximum_resistance=10kΩ package=THT]
  R2 = Resistor [tolerance=±5% resistance=330 package="0603 [SMD]"]
  LED1 = LED - 5mm [color="Red (633nm)" package="5 mm [THT]"]

nets:
  N1: パーツ1.A0, R1.wiper
  N2: パーツ1.D3_PWM, R2.Pin_0
  N3: パーツ1.5V, R1.leg1
  N4: パーツ1.GND, R1.leg2, LED1.cathode
  N5: R2.Pin_1, LED1.anode
