# Fritzing sketch bread (saved by Fritzing 0.9.3b)
breadboards: 1

parts:
  パーツ1 = Arduino Uno (Rev3)
  LED1 = LED - 5mm [color="Red (633nm)" package="5 mm [THT]"]
  R2 = Resistor [tolerance=±5% resistance=330 package=THT]
  R3 = Resistor [tolerance=±5% resistance=330 package=THT]
  LED2 = LED - 5mm [color="Red (633nm)" package="5 mm [THT]"]
  R4 = PHOTOCELL [package=photocell]
  R5 = Resistor [tolerance=±5% resistance=10k package=THT]
  R6 = Resistor [tolerance=±5% resistance=10k package=THT]
  S1 = Momentary Switch [package=ksa_sealed_tac_switch]

nets:
  N1: パーツ1.A0, R4.P$2, R5.Pin_0
  N2: パーツ1.D2, R6.Pin_1, S1.3
  N3: パーツ1.5V, R4.P$1, R6.Pin_0
  N4: パーツ1.GND, LED1.cathode, LED2.cathode, R5.Pin_1, S1.2
  N5: LED1.anode, R2.Pin_1
  N6: R3.Pin_1, LED2.anode
