# Fritzing sketch kadai7-1-1 (saved by Fritzing 0.9.3b)
breadboards: 1

parts:
  パーツ1 = Arduino Uno (Rev3)
  パーツ2 = SRF05 Ultrasonic Rangefinder

nets:
  N1: パーツ1.D8, パーツ2.Echo
  N2: パーツ1.D7, パーツ2.Trig
  5V: パーツ1.5V, パーツ2.VCC
  GND: パーツ1.GND, パーツ2.GND
