# Fritzing sketch kadai7-1-5 (saved by Fritzing 0.9.3b)
breadboards: 1

parts:
  パーツ1 = Arduino Uno (Rev3)
  J1 = Basic Servo
  R1 = Trimmer Potentiometer [maximum_resistance=10kΩ package=THT]

nets:
  N1: パーツ1.A0, R1.wiper
  N2: パーツ1.D10_PWM/SS, J1.pulse
  5V: パーツ1.5V, J1.vcc, R1.leg1
  GND: パーツ1.GND, J1.gnd, R1.leg2
