# Fritzing sketch kadai2-1-6 (saved by Fritzing 0.9.3b)
breadboards: 1

parts:
  パーツ1 = Arduino Uno (Rev3)
  R1 = Resistor [tolerance=±5% resistance=330 package=THT]
  LED1 = LED - 5mm [color="Red (633nm)" package="5 mm [THT]"]

nets:
  N1: パーツ1.5V, R1.Pin_0
  N2: パーツ1.GND, LED1.cathode
  N3: R1.Pin_1, LED1.anode
